// Digital circuit Prueba1_Digital.dig as structural Verilog
module Prueba1_Digital (
  input  A,
  input  B,
  input  C,
  input  X,
  input  Y_2,
  input  S,
  output Y,
  output Cout
);

  wire _7408_1_pin3, _7408_1_pin11, and_1_out, and_2_out, not_1_out, not_2_out;

  not not_1 (not_1_out, C);
  and and_1 (and_1_out, A, not_1_out);
  and and_2 (and_2_out, B, C);
  or or_1 (Y, and_1_out, and_2_out);
  not not_2 (not_2_out, S);
  _7408 _7408_1 (
    .pin1(X), .pin2(not_2_out), .pin3(_7408_1_pin3), .pin7(1'b0), .pin11(_7408_1_pin11), .pin12(Y_2),
    .pin13(S), .pin14(1'b1));  // open: pin4, pin5, pin6, pin8, pin9, pin10
  _7432 _7432_1 (
    .pin1(_7408_1_pin3), .pin2(_7408_1_pin11), .pin3(Cout), .pin7(1'b0), .pin14(1'b1));  // open: pin4, pin5, pin6, pin8, pin9, pin10, pin11, pin12, pin13

  // Other names for the same wires on the sheet: A_t = X; B_t = Y_2; C_t = S
endmodule
